// Digital circuit solution.dig as structural Verilog
module solution (
  input  reset,
  input  [7:0] M,
  input  start,
  input  clock,
  input  [7:0] N,
  output [15:0] Z,
  output busy,
  output [15:0] out_8,
  output [15:0] out_9
);

  wire and_1_out, and_2_out, and_3_out, and_5_out, comparator_1_gt, d_ff_1_q, multiplexer_1_out, or_1_out,
       run;
  wire [15:0] add_1_s, add_2_s, add_3_s, div_1_r, M_c_plus_2, multiplexer_2_out, multiplexer_3_out,
       multiplexer_4_out, multiplexer_5_out, multiplexer_6_out, multiplexer_8_out, N_c, Sum_p;

  Multiplexer multiplexer_1 (.sel(reset), .in_0(start), .in_1(1'b0), .out(multiplexer_1_out));
  Comparator #(.Bits(16)) comparator_1 (.a(out_8), .b(N_c), .gt(comparator_1_gt));  // open: eq, lt
  D_FF d_ff_1 (.D(multiplexer_1_out), .C(clock), .Q(d_ff_1_q));  // open: nQ
  and and_1 (and_1_out, ~d_ff_1_q, start);  // And
  Add #(.Bits(16)) add_1 (.a(out_8), .b(16'h2), .c_i(1'b0), .s(add_1_s));  // open: c_o
  and and_2 (and_2_out, busy, ~comparator_1_gt);  // And
  and and_3 (and_3_out, busy, ~comparator_1_gt);  // And
  Multiplexer #(.Bits(16)) multiplexer_2 (.sel(comparator_1_gt), .in_0(Z), .in_1(out_9), .out(multiplexer_2_out));
  Add #(.Bits(16)) add_2 (.a({{8{1'b0}}, M}), .b(16'h1), .c_i(1'b0), .s(add_2_s));  // open: c_o
  Div #(.Bits(16)) div_1 (.a({{8{1'b0}}, M}), .b(16'h2), .r(div_1_r));  // open: q
  Multiplexer #(.Bits(16)) multiplexer_3 (
    .sel(reset), .in_0(multiplexer_2_out), .in_1({16{1'b0}}), .out(multiplexer_3_out));
  Multiplexer #(.Bits(16)) multiplexer_4 (
    .sel(div_1_r[0]), .in_0({{8{1'b0}}, M}), .in_1(add_2_s), .out(multiplexer_4_out));
  and and_4 (run, ~busy, and_1_out);  // And
  or or_1 (or_1_out, run, and_3_out);
  D_FF #(.Bits(16)) d_ff_2 (.D(multiplexer_3_out), .C(clock), .Q(Z));  // open: nQ
  Multiplexer #(.Bits(16)) multiplexer_5 (.sel(run), .in_0(N_c), .in_1({{8{1'b0}}, N}), .out(multiplexer_5_out));
  D_FF #(.Bits(16)) d_ff_3 (.D(multiplexer_5_out), .C(clock), .Q(N_c));  // open: nQ
  Multiplexer #(.Bits(16)) multiplexer_6 (
    .sel(run), .in_0(M_c_plus_2), .in_1(multiplexer_4_out), .out(multiplexer_6_out));
  Multiplexer #(.Bits(16)) multiplexer_7 (.sel(and_2_out), .in_0(out_8), .in_1(add_1_s), .out(M_c_plus_2));
  D_FF #(.Bits(16)) d_ff_4 (.D(multiplexer_6_out), .C(clock), .Q(out_8));  // open: nQ
  Multiplexer #(.Bits(16)) multiplexer_8 (.sel(run), .in_0(Sum_p), .in_1({16{1'b0}}), .out(multiplexer_8_out));
  and and_5 (and_5_out, ~reset, or_1_out);  // And
  D_FF #(.Bits(16)) d_ff_5 (.D(multiplexer_8_out), .C(clock), .Q(out_9));  // open: nQ
  Add #(.Bits(16)) add_3 (.a(out_9), .b(out_8), .c_i(1'b0), .s(add_3_s));  // open: c_o
  D_FF d_ff_6 (.D(and_5_out), .C(clock), .Q(busy));  // open: nQ
  Multiplexer #(.Bits(16)) multiplexer_9 (.sel(and_2_out), .in_0(out_9), .in_1(add_3_s), .out(Sum_p));

  // Other names for the same wires on the sheet: clk = clock; M_t[7:0] = M; M_c[15:0] = out_8; N_t[7:0] = N;
  //   R = reset; S = start; Sum_c[15:0] = out_9; Z_m[15:0] = Z
endmodule

/* Test case T01:
 M  N start clock reset Z busy
 0  0 0     0     1     x x
 0  0 0     1     1     x 0
 0  0 0     0     1     x 0
 0  0 0     1     1     x 0
 1 10 1     0     0     x 0
 1 10 1     1     0     x 1
 0  0 0     0     0     x 1
 0  0 0     1     0     x 1
 0  0 0     0     0     x 1
 0  0 0     1     0     x 1
 0  0 0     0     0     x 1
 0  0 0     1     0     x x
 0  0 0     0     0     x x
 0  0 0     1     0     x x
 0  0 0     0     0     x x
 0  0 0     1     0     x x
 0  0 0     0     0     x x
 0  0 0     1     0     x x
 0  0 0     0     0     x x
 0  0 0     1     0     x x
 0  0 0     0     0     x x
 0  0 0     1     0     x x
 0  0 0     0     0     x x
 0  0 0     1     0     x x
 0  0 0     0     0     x x
 0  0 0     1     0     x x
 0  0 0     0     0     x x
 0  0 0     1     0     x x
 0  0 0     0     0     x x
 0  0 0     1     0     x x
 0  0 0     0     0     x x
 0  0 0     1     0     x x
 0  0 0     0     0     x x
 0  0 0     1     0     x x
 0  0 0     0     0     x x
 0  0 0     1     0     x x
 0  0 0     0     0     x x
 0  0 0     1     0     x x
 0  0 0     0     0     x x
 0  0 0     1     0     x x
 0  0 0     0     0     x x
 0  0 0     1     0     x x
 0  0 0     0     0     x x
 0  0 0     1     0     x x
 0  0 0     0     0     x x
 0  0 0     1     0     x x
 0  0 0     0     0     x x
 0  0 0     1     0     x x
 0  0 0     0     0     x x
 0  0 0     1     0     x x
 0  0 0     0     0     x x
 0  0 0     1     0     x x
 0  0 0     0     0     x x
 0  0 0     1     0     x x
 0  0 0     0     0     x x
 0  0 0     1     0     x x
 0  0 0     0     0     x x
 0  0 0     1     0     x x
 0  0 0     0     0     x x
 0  0 0     1     0     x x
 0  0 0     0     0     x x
 0  0 0     1     0     x x
 0  0 0     0     0     x x
 0  0 0     1     0     x x
 0  0 0     0     0     x x
 0  0 0     1     0     x x
 0  0 0     0     0     x x
 0  0 0     1     0     x x
 0  0 0     0     0     x x
 0  0 0     1     0     x x
 0  0 0     0     0     x x
 0  0 0     1     0     x x
 0  0 0     0     0     x x
 0  0 0     1     0     x x
 0  0 0     0     0     x x
 0  0 0     1     0     x x
 0  0 0     0     0     x x
 0  0 0     1     0     x x
 0  0 0     0     0     x x
 0  0 0     1     0     x x
 0  0 0     0     0     x x
 0  0 0     1     0     x x
 0  0 0     0     0     x x
 0  0 0     1     0     x x
 0  0 0     0     0     x x
 0  0 0     1     0     x x
 0  0 0     0     0     x x
 0  0 0     1     0     x x
 0  0 0     0     0     x x
 0  0 0     1     0     x x
 0  0 0     0     0     x x
 0  0 0     1     0     x x
 0  0 0     0     0     x x
 0  0 0     1     0     x x
 0  0 0     0     0     x x
 0  0 0     1     0     x x
 0  0 0     0     0     x x
 0  0 0     1     0     x x
 0  0 0     0     0     x x
 0  0 0     1     0     x x
 0  0 0     0     0     x x
 0  0 0     1     0     x x
 0  0 0     0     0     x x
 0  0 0     1     0     x x
 0  0 0     0     0     x x
 0  0 0     1     0     x x
 0  0 0     0     0     x x
 0  0 0     1     0     x x
 0  0 0     0     0     x x
 0  0 0     1     0     x x
 0  0 0     0     0     x x
 0  0 0     1     0     x x
 0  0 0     0     0     x x
 0  0 0     1     0     x x
 0  0 0     0     0     30 0
 0  0 0     1     0     30 0
 0  0 0     0     0     30 0
 0  0 0     1     0     30 0
*/
