// Digital circuit solution.dig as structural Verilog
module solution (
  input  CH,
  input  CL,
  input  MH,
  input  QL,
  input  MT,
  input  AD,
  output UP,
  output DN,
  output AL
);

  wire and_1_out, and_2_out, and_3_out, and_4_out, and_5_out, and_6_out, and_7_out, and_8_out, not_1_out,
       not_2_out, not_3_out, not_4_out, not_5_out, not_6_out, not_7_out, or_1_out;

  not not_1 (not_1_out, CH);
  not not_2 (not_2_out, CL);
  not not_3 (not_3_out, MH);
  not not_4 (not_4_out, QL);
  not not_5 (not_5_out, MT);
  not not_6 (not_6_out, AD);
  and and_1 (and_1_out, CH, MH);
  and and_2 (and_2_out, CH, QL);
  and and_3 (and_3_out, MH, QL);
  and and_4 (and_4_out, CL, not_5_out);
  and and_5 (and_5_out, CH, MH, QL);
  and and_6 (and_6_out, MT, or_1_out);
  or or_1 (or_1_out, and_1_out, and_2_out, and_3_out);
  or or_2 (AL, and_5_out, and_7_out);
  and and_7 (and_7_out, and_6_out, not_6_out);
  and and_8 (and_8_out, or_1_out, not_5_out);
  not not_7 (not_7_out, UP);
  and and_9 (DN, not_7_out, and_4_out);
  or or_3 (UP, and_8_out, AD);

  // Notes on the sheet:
  //   UP: Scale Up
  //   DN: Scale Down
  //   AL: Alert
  //   Don't change anything inside this box
endmodule

/* Test case T1:
CH CL MH QL MT AD UP DN AL
0 0 0 0 0 0 0 0 0
1 0 0 1 0 0 1 0 0
0 1 0 0 0 0 0 1 0
1 0 1 1 0 0 1 0 1
1 0 0 1 1 0 0 0 1
0 0 0 0 0 1 1 0 0
*/
